# Fritzing sketch schema (saved by Fritzing 0.9.10b)
breadboards: 1

parts:
  Composant1 = Arduino Mega 2560 (Rev3)
  microSD1 = MicroSD Card Module
  LCD2004-I2C1 = LCD2004-I2C

nets:
  N1: Composant1.D21/SCL, LCD2004-I2C1.SCL
  N2: Composant1.D20/SDA, LCD2004-I2C1.SDA
  VCC: Composant1.5V, microSD1.VCC, LCD2004-I2C1.VCC
  GND: Composant1.GND, microSD1.GND, LCD2004-I2C1.GND

custom parts:
  LCD2004-I2C: A standard character display with 4x20 characters. Comes in many colors with LCM2004 IIC attached.
