# Fritzing sketch schema (saved by Fritzing 0.9.10b)
breadboards: 1
perfboards: 1

parts:
  Composant1 = Arduino Mega 2560 (Rev3)
  microSD1 = MicroSD Card Module
  LCD2004-I2C1 = LCD2004-I2C
  S1 = Pushbutton [package="[THT]"]
  S2 = Pushbutton [package="[THT]"]
  S3 = Pushbutton [package="[THT]"]
  S4 = Pushbutton [package="[THT]"]
  Composant2 = HX711 Weighing Sensor Module
  S5 = Load Sensor - 50kg [part_number=SEN-10245]
  S6 = Load Sensor - 50kg [part_number=SEN-10245]
  S7 = Load Sensor - 50kg [part_number=SEN-10245]
  S8 = Load Sensor - 50kg [part_number=SEN-10245]

nets:
  N1: Composant1.A4, LCD2004-I2C1.SDA
  N2: Composant1.A5, LCD2004-I2C1.SCL
  N3: Composant1.D13_PWM, microSD1.SCK
  N4: Composant1.D12_PWM, microSD1.MISO
  N5: Composant1.D11_PWM, microSD1.MOSI
  N6: Composant1.D10_PWM, microSD1.CS
  VCC: Composant1.5V, microSD1.VCC, LCD2004-I2C1.VCC, Composant2.VCC
  GND: Composant1.GND, microSD1.GND, LCD2004-I2C1.GND, Composant2.GND
  N7: Composant1.D4_PWM, Composant2.DO/RX
  N8: Composant1.D5_PWM, Composant2.CK/TX
  N9: S1.Pin_1, S1.Pin_2
  N10: S1.Pin_3, S1.Pin_4
  N11: S2.Pin_1, S2.Pin_2
  N12: S2.Pin_3, S2.Pin_4
  N13: S3.Pin_1, S3.Pin_2
  N14: S3.Pin_3, S3.Pin_4
  N15: S4.Pin_1, S4.Pin_2
  N16: S4.Pin_3, S4.Pin_4
  N17: Composant2.E+, S5.R
  N18: Composant2.E-, S8.R
  N19: Composant2.A+, S7.R
  N20: Composant2.A-, S6.R
  N21: S5.B, S7.B
  N22: S5.W, S6.W
  N23: S6.B, S8.B
  N24: S7.W, S8.W

custom parts:
  LCD2004-I2C: A standard character display with 4x20 characters. Comes in many colors with LCM2004 IIC attached.
  Load Sensor - 50kg: Half-wheatstone bridge Load Cell modified from the Fritzing Repo This load sensor, sometimes called a strain gauge, is the same one found in digital bathroom scales (you know, the ones you use in January for your New Year's resolutions, and then forget about a month later). This sensor can measure up to about 110 pounds.
